# Fritzing sketch IRDetect (saved by Fritzing 0.9.6b)

parts:
  Part1 = Arduino Uno (Rev3)
  Grove1 = Grove Infrared Receiver

nets:
  N1: Part1.D11_PWM/MOSI, Grove1.RX
  5V: Part1.5V, Grove1.VCC
  GND: Part1.GND, Grove1.GND
